# Fritzing sketch LM35DZ (saved by Fritzing 0.9.2b)
breadboards: 1

parts:
  Componente1 = Arduino Uno (Rev3)
  T1 = LM35 Temperature Sensor [package="TO92 [THT]"]
  U1 = LCD-16X2 [package=lcd-16x2_noholes]  # not connected

nets:
  N1: Componente1.A3, T1.Vout
